// Digital circuit main.dig as structural Verilog
module main (
  input  [7:0] Instruction_Binary,
  input  clk,
  input  Turn_on_button,
  input  [7:0] Starting_address,
  input  in_6,
  output [7:0] out_2
);

  wire [7:0] u_counter_8bit_count;

  counter_8bit #(.applicationType("IVERILOG"), .CodeFile("/home/kaldwin/Development/Projects/the_electronics_project_misc/src/counter_8bit.v")) u_counter_8bit (
    .clk(clk), .num(Starting_address), .load(in_6), .count(u_counter_8bit_count));
  memory_256x8 #(.applicationType("IVERILOG"), .CodeFile("/home/kaldwin/Development/Projects/the_electronics_project_misc/src/memory_256x8.v")) u_memory_256x8 (
    .clk(clk), .write(Turn_on_button), .address(u_counter_8bit_count), .data_in(Instruction_Binary),
    .data_out(out_2));

  // Notes on the sheet:
  //   clk: Hz: 5
endmodule
